# Fritzing sketch simple_button_schematic (saved by Fritzing 1.0.0rc)
breadboards: 1

parts:
  LED1 = smd LED [color="Red (633nm)" package="1206 [SMD]"]
  R1 = Resistor [tolerance=±5% resistance=220 package="2010 [SMD]"]
  S1 = Pushbutton [package="[THT]"]
  M1 = ESP32-S2-DevKitC-1 [part_number=ESP32-S2-DevKitC-1]

nets:
  N1: LED1.cathode, S1.Pin_3, S1.Pin_4, M1.pin_22, M1.pin_23
  N2: LED1.anode, R1.Pin_1
  N3: R1.Pin_0, M1.pin_5
  N4: S1.Pin_1, S1.Pin_2, M1.pin_4

custom parts:
  ESP32-S2-DevKitC-1: ESP32-S2-DevKitC-1 is an entry-level development board based on ESP32-S2-SOLO (on-board PCB antenna). It is based on the ESP32 microcontroller that boasts Wifi, Bluetooth, Ethernet and Low Power support all in a single chip. (vanepp) Feb 2022: converted to ESP32-S2-DevKitC-1. This module is 44pins long (2x22) and 11 pins width.
