# Fritzing sketch adafruit-gps-current-testing (saved by Fritzing 1.0.0rc)

parts:
  M1 = ESP32-S2-DevKitC-1 [part_number=ESP32-S2-DevKitC-1]
  Part1 = Adafruit Ultimate GPS v3 [part_number="Adafruit #746"]
  Power_plug1 = Power plug
  AM1 = Multimeter (DC Current)

nets:
  N1: M1.pin_12, Part1.ENABLE
  N2: M1.pin_15, Part1.TX
  N3: M1.pin_16, Part1.RX
  GND: M1.pin_22, Part1.GND, Power_plug1.GND
  N4: Part1.VIN, AM1.COM_Probe
  N5: Power_plug1.VCC, AM1.A_Probe

custom parts:
  ESP32-S2-DevKitC-1: ESP32-S2-DevKitC-1 is an entry-level development board based on ESP32-S2-SOLO (on-board PCB antenna). It is based on the ESP32 microcontroller that boasts Wifi, Bluetooth, Ethernet and Low Power support all in a single chip. (vanepp) Feb 2022: converted to ESP32-S2-DevKitC-1. This module is 44pins long (2x22) and 11 pins width.
  Adafruit Ultimate GPS v3: We carry a few different GPS modules here in the Adafruit shop, but none that satisfied our every desire - that's why we designed this little GPS breakout board. We believe this is the Ultimate GPS module, so we named it that. It's got everything you want and more: -165 dBm sensitivity, 10 Hz updates, 66 channels 5V friendly design and only 20mA current draw Breadboard friendly + two mounting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
